# Fritzing sketch stepper (saved by Fritzing 0.8.7b)
breadboards: 1

parts:
  M1 = Stepper Motor - Bipolar
  M2 = Stepper Motor - Bipolar
  A1 = A4988
  A2 = A4988
  Raspberry_Pi_1 = Raspberry Pi 3
  C1 = Electrolytic Capacitor [capacitance=47µF package="100 mil [THT, electrolytic]"]
  U1 = LIPO-2000mAh [package=lipo-2000]
  U2 = LIPO-2000mAh [package=lipo-2000]
  U3 = LIPO-2000mAh [package=lipo-2000]

nets:
  N1: M1.A, A1.2B
  N2: M1.C, A1.2A
  N3: M1.B, A1.1A
  N4: M1.D, A1.1B
  N5: M2.A, A2.2B
  N6: M2.C, A2.2A
  N7: M2.B, A2.1A
  N8: M2.D, A2.1B
  N9: A1.GND#13, A2.GND#13, Raspberry_Pi_1.GND
  VDD: A1.VDD, A2.VDD, Raspberry_Pi_1.5V
  N10: A1.GND#19, A2.GND#19, C1.-, U3.-
  N11: A1.VMOT, A2.VMOT, C1.+, U1.+
  N12: A1.DIRECTION, Raspberry_Pi_1.GIPO24
  N13: A1.STEP, A2.STEP, Raspberry_Pi_1.GIPO23
  N14: A1.SLEEP, A1.RESET
  N15: A2.DIRECTION, Raspberry_Pi_1.GIPO25
  N16: A2.SLEEP, A2.RESET
  N17: U1.-, U2.+
  N18: U2.-, U3.+
